// Logisim project logisim_4_bit_adder.circ as structural Verilog: 1 circuit, main circuit main
module main (
  input  a,
  input  in_2,
  input  in_3,
  input  in_4,
  input  in_5,
  input  in_6,
  input  in_7,
  input  in_8,
  input  in_9,
  input  b,
  input  in1,
  input  in2,
  input  Cin
);

  wire and_1_out, and_2_out, and_3_out, and_4_out, and_5_out, and_6_out, and_7_out, and_8_out, and_9_out,
       and_10_out, or_1_out, or_2_out, or_3_out, or_4_out, xor_1_out, xor_2_out, xor_3_out, xor_4_out,
       xor_5_out, xor_6_out, xor_7_out, xor_8_out, xor_9_out, xor_10_out;

  and and_1 (and_1_out, a, b);
  xor xor_1 (xor_1_out, a, b);
  and and_2 (and_2_out, in1, in2);
  xor xor_2 (xor_2_out, in1, in2);
  and and_3 (and_3_out, xor_2_out, Cin);
  xor xor_3 (xor_3_out, xor_2_out, Cin);
  or or_1 (or_1_out, and_2_out, and_3_out);
  and and_4 (and_4_out, in_2, in_6);
  xor xor_4 (xor_4_out, in_2, in_6);
  and and_5 (and_5_out, in_3, in_7);
  xor xor_5 (xor_5_out, in_3, in_7);
  and and_6 (and_6_out, in_4, in_8);
  xor xor_6 (xor_6_out, in_4, in_8);
  and and_7 (and_7_out, in_5, in_9);
  xor xor_7 (xor_7_out, in_5, in_9);
  and and_8 (and_8_out, xor_4_out, or_3_out);
  xor xor_8 (xor_8_out, xor_4_out, or_3_out);
  and and_9 (and_9_out, xor_5_out, or_4_out);
  xor xor_9 (xor_9_out, xor_5_out, or_4_out);
  and and_10 (and_10_out, xor_6_out, and_7_out);
  xor xor_10 (xor_10_out, xor_6_out, and_7_out);
  or or_2 (or_2_out, and_4_out, and_8_out);
  or or_3 (or_3_out, and_5_out, and_9_out);
  or or_4 (or_4_out, and_6_out, and_10_out);
  LED overflow (.in(or_2_out));
  LED led_1 (.in(xor_8_out));
  LED led_2 (.in(xor_9_out));
  LED led_3 (.in(xor_10_out));
  LED led_4 (.in(xor_7_out));
endmodule
