// Logisim project OR.circ as structural Verilog: 1 circuit, main circuit main
module main (
  input  in_1,
  input  in_2
);

  wire and_1_out, and_2_out, nand_1_out, nand_2_out, nand_3_out, nand_4_out, not_1_out, not_2_out;

  not not_1 (not_1_out, in_1);
  not not_2 (not_2_out, in_2);
  nand nand_1 (nand_1_out, not_1_out, in_2);
  nand nand_2 (nand_2_out, in_2, in_1);
  nand nand_3 (nand_3_out, in_1, not_2_out);
  and and_1 (and_1_out, nand_1_out, nand_2_out);
  and and_2 (and_2_out, nand_2_out, nand_3_out);
  nand nand_4 (nand_4_out, and_1_out, and_2_out);
  LED led_1 (.in(nand_4_out));

  // Notes on the sheet:
  //   I don't think it's the best solution, but I'm proud of it.
endmodule
