// Logisim project MULTI_BIT_NOT.circ as structural Verilog
module not_32bit (
  input  in_01,
  input  in_02,
  input  in_03,
  input  in_04,
  input  in_05,
  input  in_06,
  input  in_07,
  input  in_08,
  input  in_09,
  input  in_10,
  input  in_11,
  input  in_12,
  input  in_13,
  input  in_14,
  input  in_15,
  input  in_16,
  input  in_17,
  input  in_18,
  input  in_19,
  input  in_20,
  input  in_21,
  input  in_22,
  input  in_23,
  input  in_24,
  input  in_25,
  input  in_26,
  input  in_27,
  input  in_28,
  input  in_29,
  input  in_30,
  input  in_31,
  input  in_32,
  output out_01,
  output out_02,
  output out_03,
  output out_04,
  output out_05,
  output out_06,
  output out_07,
  output out_08,
  output out_09,
  output out_10,
  output out_11,
  output out_12,
  output out_13,
  output out_14,
  output out_15,
  output out_16,
  output out_17,
  output out_18,
  output out_19,
  output out_20,
  output out_21,
  output out_22,
  output out_23,
  output out_24,
  output out_25,
  output out_26,
  output out_27,
  output out_28,
  output out_29,
  output out_30,
  output out_31,
  output out_32
);

  not not_1 (out_01, in_01);
  not not_2 (out_02, in_02);
  not not_3 (out_03, in_03);
  not not_4 (out_04, in_04);
  not not_5 (out_05, in_05);
  not not_6 (out_06, in_06);
  not not_7 (out_07, in_07);
  not not_8 (out_08, in_08);
  not not_9 (out_09, in_09);
  not not_10 (out_10, in_10);
  not not_11 (out_11, in_11);
  not not_12 (out_12, in_12);
  not not_13 (out_13, in_13);
  not not_14 (out_14, in_14);
  not not_15 (out_15, in_15);
  not not_16 (out_16, in_16);
  not not_17 (out_17, in_17);
  not not_18 (out_18, in_18);
  not not_19 (out_19, in_19);
  not not_20 (out_20, in_20);
  not not_21 (out_21, in_21);
  not not_22 (out_22, in_22);
  not not_23 (out_23, in_23);
  not not_24 (out_24, in_24);
  not not_25 (out_25, in_25);
  not not_26 (out_26, in_26);
  not not_27 (out_27, in_27);
  not not_28 (out_28, in_28);
  not not_29 (out_29, in_29);
  not not_30 (out_30, in_30);
  not not_31 (out_31, in_31);
  not not_32 (out_32, in_32);
endmodule
