// Logisim project CLOCKED_D_LATCH.circ as structural Verilog: 1 circuit, main circuit main
module main (
  input  DATA
);

  wire and_1_out, CLK_out, nand_1_out, nand_2_out, nand_3_out, nand_4_out, not_1_out, not_2_out, not_3_out;

  Clock CLK (.out(CLK_out));
  not not_1 (not_1_out, CLK_out);
  not not_2 (not_2_out, not_1_out);
  not not_3 (not_3_out, not_2_out);
  and and_1 (and_1_out, CLK_out, not_3_out);
  nand nand_1 (nand_1_out, DATA, and_1_out);
  nand nand_2 (nand_2_out, nand_1_out, and_1_out);
  nand nand_3 (nand_3_out, nand_1_out, nand_4_out);
  nand nand_4 (nand_4_out, nand_3_out, nand_2_out);
  LED Q (.in(nand_3_out));
  LED NOT_Q (.in(nand_4_out));
endmodule
