// Logisim project D_TYPE_FLIP_FLOP.circ as structural Verilog: 1 circuit, main circuit main
module main (
  input  DATA
);

  wire CLK_out, nand_1_out, nand_2_out, nand_3_out, nand_4_out, nand_5_out, nand_6_out, nand_7_out,
       nand_8_out, not_1_out;

  Clock CLK (.out(CLK_out));
  nand nand_1 (nand_1_out, DATA, CLK_out);
  nand nand_2 (nand_2_out, nand_1_out, CLK_out);
  not not_1 (not_1_out, CLK_out);
  nand nand_3 (nand_3_out, nand_1_out, nand_4_out);
  nand nand_4 (nand_4_out, nand_3_out, nand_2_out);
  nand nand_5 (nand_5_out, nand_3_out, not_1_out);
  nand nand_6 (nand_6_out, not_1_out, nand_4_out);
  nand nand_7 (nand_7_out, nand_5_out, nand_8_out);
  nand nand_8 (nand_8_out, nand_7_out, nand_6_out);
  LED Q (.in(nand_7_out));
  LED NOT_Q (.in(nand_8_out));
endmodule
