// Logisim project GATED_SR_LATCH_NAND.circ as structural Verilog: 1 circuit, main circuit main
module main (
  input  SET,
  input  ENABLE,
  input  RESET
);

  wire nand_1_out, nand_2_out, nand_3_out, nand_4_out;

  nand nand_1 (nand_1_out, SET, ENABLE);
  nand nand_2 (nand_2_out, ENABLE, RESET);
  nand nand_3 (nand_3_out, nand_1_out, nand_4_out);
  nand nand_4 (nand_4_out, nand_3_out, nand_2_out);
  LED Q (.in(nand_3_out));
  LED NOT_Q (.in(nand_4_out));
endmodule
