// Logisim project GATED_SR_LATCH_NOR.circ as structural Verilog: 1 circuit, main circuit main
module main (
  input  RESET,
  input  ENABLE,
  input  SET
);

  wire and_1_out, and_2_out, nor_1_out, nor_2_out;

  and and_1 (and_1_out, RESET, ENABLE);
  and and_2 (and_2_out, ENABLE, SET);
  nor nor_1 (nor_1_out, and_1_out, nor_2_out);
  nor nor_2 (nor_2_out, nor_1_out, and_2_out);
  LED Q (.in(nor_1_out));
  LED NOT_Q (.in(nor_2_out));
endmodule
