// Logisim project SR_LATCH_NAND.circ as structural Verilog: 1 circuit, main circuit main
module main (
  input  SET,
  input  RESET
);

  wire nand_1_out, nand_2_out;

  nand nand_1 (nand_1_out, SET, nand_2_out);
  nand nand_2 (nand_2_out, nand_1_out, RESET);
  LED Q (.in(nand_1_out));
  LED NOT_Q (.in(nand_2_out));
endmodule
