// Logisim project SR_LATCH_NOR.circ as structural Verilog: 1 circuit, main circuit main
module main (
  input  RESET,
  input  SET
);

  wire nor_1_out, nor_2_out;

  nor nor_1 (nor_1_out, RESET, nor_2_out);
  nor nor_2 (nor_2_out, nor_1_out, SET);
  LED Q (.in(nor_1_out));
  LED NOT_Q (.in(nor_2_out));
endmodule
