// Logisim project TRAFFIC_LIGHTS.circ as structural Verilog: 1 circuit, main circuit main
module main (
  input  T_A,
  input  T_B
);

  wire and_1_out, and_2_out, and_3_out, and_4_out, CLK_out, not_1_out, not_2_out, not_3_out, not_4_out,
       not_5_out, not_6_out, not_7_out;
  wire [1:0] STATE_REGISTER_q, xor_1_out;

  Clock #(.highDuration(4)) CLK (.out(CLK_out));
  not not_1 (not_1_out, STATE_REGISTER_q[0]);
  not not_2 (not_2_out, STATE_REGISTER_q[1]);
  not not_3 (not_3_out, T_A);
  not not_4 (not_4_out, STATE_REGISTER_q[1]);
  not not_5 (not_5_out, T_B);
  xor xor_1 (xor_1_out[0], STATE_REGISTER_q[0], STATE_REGISTER_q[1]);
  and and_1 (and_1_out, not_1_out, not_2_out, not_3_out);
  and and_2 (and_2_out, STATE_REGISTER_q[0], not_4_out, not_5_out);
  or or_1 (xor_1_out[1], and_1_out, and_2_out);
  Register #(.width(2)) STATE_REGISTER (.D(xor_1_out), .clk(CLK_out), .Q(STATE_REGISTER_q));  // open: en, clr
  not not_6 (not_6_out, STATE_REGISTER_q[0]);
  not not_7 (not_7_out, STATE_REGISTER_q[0]);
  and and_3 (and_3_out, not_6_out, STATE_REGISTER_q[1]);
  and and_4 (and_4_out, STATE_REGISTER_q[0], STATE_REGISTER_q[1]);
  LED L_A1 (.in(STATE_REGISTER_q[0]));
  LED L_A0 (.in(and_3_out));
  LED L_B1 (.in(not_7_out));
  LED L_B0 (.in(and_4_out));

  // Notes on the sheet:
  //   NEXT STATE LOGIC
  //   OUTPUT LOGIC
  //   OUTPUTS
endmodule
